// Logisim project Logisim Circuit.circ as structural Verilog: 1 circuit, main circuit Logisim Circuit
module Logisim_Circuit (
  input  C,
  input  T,
  input  F,
  input  R,
  output A
);

  wire and_1_out, comparator_1_eq, comparator_1_gt, comparator_2_gt, comparator_3_gt, comparator_4_gt,
       or_1_out;

  Comparator comparator_1 (.a(8'h5), .b({8{1'b0}}), .gt(comparator_1_gt), .eq(comparator_1_eq), .lt(comparator_1_gt));
  Comparator comparator_2 (.a(8'h5), .b({8{1'b0}}), .gt(comparator_2_gt), .eq(comparator_2_gt), .lt(comparator_2_gt));
  Comparator comparator_3 (.a(8'h5), .b({8{1'b0}}), .gt(comparator_3_gt), .eq(comparator_3_gt), .lt(comparator_3_gt));
  Comparator #(.mode("unsigned")) comparator_4 (
    .a(8'h5), .b({8{1'b0}}), .gt(comparator_4_gt), .eq(comparator_4_gt), .lt(comparator_4_gt));
  and and_1 (and_1_out, F, F, R);
  or or_1 (or_1_out, C, and_1_out);

  assign T = F;
endmodule
